// Logisim project VHDL_1.circ as structural Verilog
module Q1_logic4 (
  input  a,
  input  b,
  input  c,
  input  d,
  output out1,
  output out2
);

  and and_1 (out1, a, b, c, d);
  or or_1 (out2, a, b, c, d);
endmodule

module Q2_mux8 (
  input  a,
  input  e,
  input  b,
  input  f,
  input  c,
  input  g,
  input  d,
  input  h,
  input  [2:0] sel,
  output data
);

  Multiplexer #(.select(3)) multiplexer_1 (
    .in0(a), .in1(b), .in2(c), .in3(d), .in4(e), .in5(f), .in6(g), .in7(h), .out(data), .sel(sel));
endmodule

module Q3_letters7seg (
  input  [2:0] dat,
  input  en,
  output [7:0] display
);

  wire [7:0] a_b_c_d_f_g_data;

  ROM #(.addrWidth(3)) a_b_c_d_f_g (.addr(dat), .data(a_b_c_d_f_g_data));
  Multiplexer #(.width(8)) multiplexer_1 (.in0({8{1'b0}}), .in1(a_b_c_d_f_g_data), .out(display), .sel(en));
  _7_Segment_Display seven_segment (
    .g(display[1]), .f(display[2]), .a(display[7]), .b(display[6]), .e(display[3]), .d(display[4]),
    .c(display[5]), .dp(display[0]));

  // Other names for the same wires on the sheet: dp = display[0]; g = display[1]; f = display[2]; e = display[3];
  //   d = display[4]; c = display[5]; b = display[6]; a = display[7]

  // Notes on the sheet:
  //   contents of a_b_c_d_f_g (hex, n*v repeats v):
  //   fa 3e 1a 7a 8e f6
endmodule

module Q4_vote25 (
  input  [24:0] vt,
  output result
);

  wire comparator_1_eq, comparator_1_gt;
  wire [4:0] bitadder_1_out;

  BitAdder #(.width(25)) bitadder_1 (.in0(vt), .out(bitadder_1_out));
  // Probe on bitadder_1_out
  Comparator #(.mode("unsigned"), .width(5)) comparator_1 (
    .a(bitadder_1_out), .b(5'b01101), .gt(comparator_1_gt), .eq(comparator_1_eq));  // open: lt
  or or_1 (result, comparator_1_gt, comparator_1_eq);
endmodule

module Q5_popcount13_7seg (
  input  [12:0] vt,
  input  en,
  output [7:0] display
);

  wire [3:0] bitadder_1_out;
  wire [7:0] hex_0_to_F_data;

  // Probe on bitadder_1_out
  BitAdder #(.width(13)) bitadder_1 (.in0(vt), .out(bitadder_1_out));
  ROM #(.addrWidth(4)) hex_0_to_F (.addr(bitadder_1_out), .data(hex_0_to_F_data));
  Multiplexer #(.width(8)) multiplexer_1 (.in0({8{1'b0}}), .in1(hex_0_to_F_data), .out(display), .sel(en));
  _7_Segment_Display seven_segment (
    .g(display[1]), .f(display[2]), .a(display[7]), .b(display[6]), .e(display[3]), .d(display[4]),
    .c(display[5]), .dp(display[0]));

  // Other names for the same wires on the sheet: dp = display[0]; g = display[1]; f = display[2]; e = display[3];
  //   d = display[4]; c = display[5]; b = display[6]; a = display[7]

  // Notes on the sheet:
  //   contents of hex_0_to_F (hex, n*v repeats v):
  //   fc 60 da f2 66 b6 be e0 fe f6 ee 3e 9c 7a 9e 8e
endmodule

module HDL_Q1 (
  input  a,
  input  b,
  input  c,
  input  d,
  output out1,
  output out2
);

  q1_logic4 q1_logic4_1 (.a(a), .b(b), .c(c), .d(d), .out1(out1), .out2(out2));
endmodule

module HDL_Q2 (
  input  a,
  input  b,
  input  c,
  input  d,
  input  e,
  input  f,
  input  g,
  input  h,
  input  [2:0] sel,
  output data
);

  q2_mux8 q2_mux8_1 (.a(a), .b(b), .c(c), .d(d), .e(e), .f(f), .g(g), .h(h), .sel(sel), .data(data));
endmodule

module HDL_Q3 (
  input  en,
  input  [2:0] dat,
  output [7:0] display
);

  q3_letters7seg q3_letters7seg_1 (.en(en), .dat(dat), .display(display));
endmodule

module HDL_Q4 (
  input  [24:0] vt,
  output result
);

  q4_vote25 q4_vote25_1 (.vt(vt), .result(result));
endmodule

module HDL_Q5 (
  input  [12:0] vt,
  input  en,
  output [7:0] display
);

  q5_popcount13_7seg q5_popcount13_7seg_1 (.vt(vt), .en(en), .display(display));
endmodule

// VHDL entity q1_logic4, as the project stores it:
-- VHDL_1, p.22, Problem 1: four-input AND and OR.
library ieee;
use ieee.std_logic_1164.all;

entity q1_logic4 is
    port (
        a, b, c, d : in std_logic;
        out1, out2 : out std_logic
    );
end q1_logic4;

architecture rtl of q1_logic4 is
begin
    out1 <= a and b and c and d;
    out2 <= a or b or c or d;
end rtl;

// VHDL entity q2_mux8, as the project stores it:
-- VHDL_1, p.22, Problem 2: eight-to-one multiplexer.
library ieee;
use ieee.std_logic_1164.all;

entity q2_mux8 is
    port (
        a, b, c, d, e, f, g, h : in std_logic;
        sel : in std_logic_vector(2 downto 0);
        data : out std_logic
    );
end q2_mux8;

architecture rtl of q2_mux8 is
begin
    process(a, b, c, d, e, f, g, h, sel)
    begin
        case sel is
            when "000" => data <= a;
            when "001" => data <= b;
            when "010" => data <= c;
            when "011" => data <= d;
            when "100" => data <= e;
            when "101" => data <= f;
            when "110" => data <= g;
            when "111" => data <= h;
            when others => data <= '0';
        end case;
    end process;
end rtl;

// VHDL entity q3_letters7seg, as the project stores it:
-- VHDL_1, p.22, Problem 3: display a, b, c, d, f, g.
-- display(7 downto 0) = a b c d e f g dp; 1 lights a segment.
-- dat: 000=a, 001=b, 010=c, 011=d, 100=f, 101=g.
library ieee;
use ieee.std_logic_1164.all;

entity q3_letters7seg is
    port (
        en : in std_logic;
        dat : in std_logic_vector(2 downto 0);
        display : out std_logic_vector(7 downto 0)
    );
end q3_letters7seg;

architecture rtl of q3_letters7seg is
begin
    process(en, dat)
    begin
        display <= "00000000";
        if en = '1' then
            case dat is
                when "000" => display <= "11111010"; -- a
                when "001" => display <= "00111110"; -- b
                when "010" => display <= "00011010"; -- c
                when "011" => display <= "01111010"; -- d
                when "100" => display <= "10001110"; -- f
                when "101" => display <= "11110110"; -- g
                when others => display <= "00000000";
            end case;
        end if;
    end process;
end rtl;

// VHDL entity q4_vote25, as the project stores it:
-- VHDL_1, p.22, Problem 4: strict majority of 25 votes.
library ieee;
use ieee.std_logic_1164.all;

entity q4_vote25 is
    port (
        vt : in std_logic_vector(24 downto 0);
        result : out std_logic
    );
end q4_vote25;

architecture rtl of q4_vote25 is
begin
    process(vt)
        variable count_ones : integer range 0 to 25;
    begin
        count_ones := 0;
        for i in vt'range loop
            if vt(i) = '1' then
                count_ones := count_ones + 1;
            end if;
        end loop;
        if count_ones >= 13 then
            result <= '1';
        else
            result <= '0';
        end if;
    end process;
end rtl;

// VHDL entity q5_popcount13_7seg, as the project stores it:
-- VHDL_1, p.22, Problem 5: 13-bit population count and display.
-- display(7 downto 0) = a b c d e f g dp; active high.
-- A 13-bit input reaches 0..13 (0..D). E/F remain in the decoder.
library ieee;
use ieee.std_logic_1164.all;

entity q5_popcount13_7seg is
    port (
        vt : in std_logic_vector(12 downto 0);
        en : in std_logic;
        display : out std_logic_vector(7 downto 0)
    );
end q5_popcount13_7seg;

architecture rtl of q5_popcount13_7seg is
    function hex_to_segments(value : natural) return std_logic_vector is
    begin
        case value is
            when 0  => return "11111100"; -- 0
            when 1  => return "01100000"; -- 1
            when 2  => return "11011010"; -- 2
            when 3  => return "11110010"; -- 3
            when 4  => return "01100110"; -- 4
            when 5  => return "10110110"; -- 5
            when 6  => return "10111110"; -- 6
            when 7  => return "11100000"; -- 7
            when 8  => return "11111110"; -- 8
            when 9  => return "11110110"; -- 9
            when 10 => return "11101110"; -- A
            when 11 => return "00111110"; -- b
            when 12 => return "10011100"; -- C
            when 13 => return "01111010"; -- d
            when 14 => return "10011110"; -- E
            when 15 => return "10001110"; -- F
            when others => return "00000000";
        end case;
    end hex_to_segments;
begin
    process(vt, en)
        variable count_ones : integer range 0 to 13;
    begin
        count_ones := 0;
        for i in vt'range loop
            if vt(i) = '1' then
                count_ones := count_ones + 1;
            end if;
        end loop;
        if en = '1' then
            display <= hex_to_segments(count_ones);
        else
            display <= "00000000";
        end if;
    end process;
end rtl;
